# Fritzing sketch shonku-robot-shield-for-arduino-uno-strip (saved by Fritzing 0.9.3b)
circuit board: 5.30319cm x 6.98894cm
stripboards: 1

parts:
  R9 = Resistor [tolerance=±5% resistance=1.5k package=THT]
  Motor_Cuttoff = Toggle Switch [part_number=S2 package=THT]
  R2 = Resistor [tolerance=±5% resistance=1k package=THT]
  C1 = Ceramic Capacitor [capacitance=100nF package="100 mil [THT, multilayer]"]
  Pow = female pin header, 8 pins [form="♀ (female)"]
  C3 = Ceramic Capacitor [capacitance=100nF package="100 mil [THT, multilayer]"]
  -_M2_+ = Header 2 [package=molex-1x2_lock]
  -_M1_+ = Header 2 [package=molex-1x2_lock]
  D8-13 = female pin header, 10 pins [form="♀ (female)"]
  J1 = male pin header, 3 pins [form="♂ (male)" part_number="Servo 1"]
  Battery_Cuttoff = Toggle Switch [part_number=S1 package=THT]
  C2 = Electrolytic Capacitor [capacitance=10µF voltage=16V package="100 mil [THT, electrolytic]"]
  J2 = male pin header, 3 pins [form="♂ (male)" part_number="Servo 2"]
  R4 = Resistor [tolerance=±5% resistance=1k package=THT]
  R1 = Resistor [tolerance=±5% resistance=10k package=THT]
  A0-5 = female pin header, 6 pins [form="♀ (female)"]
  R3 = Resistor [tolerance=±5% resistance=10k package=THT]
  C5 = Electrolytic Capacitor [capacitance=10µF voltage=16V package="100 mil [THT, electrolytic]"]
  IC2 = Voltage Regulator [part_number=7805 package=to-220-alt]
  S3 = Pushbutton [package="[THT]"]
  D0-7 = female pin header, 8 pins [form="♀ (female)"]
  IC1 = L293D [part_number=L293D package=THT]
  R7 = Resistor [tolerance=±5% resistance=10k package=THT]
  R6 = Resistor [tolerance=±5% resistance=2k package=THT]
  BLE1 = HC05 Bluetooth Module
  -_Bat_+ = Header 2 [part_number=Header package=molex-1x2_lock]
  R10 = Resistor [tolerance=±5% resistance=1.5k package=THT]
  Q2 = NPN-Transistor [part_number=2N2222A package="TO92 [THT]"]
  LED1 = LED - 3mm [color="Red (633nm)" package="3 mm [THT]"]
  Q1 = NPN-Transistor [part_number=2N2222A package="TO92 [THT]"]
  C6 = Ceramic Capacitor [capacitance=100nF package="100 mil [THT, multilayer]"]
  R13 = Resistor [tolerance=±5% resistance=1k package=THT]
  J3 = male pin header, 4 pins [form="♂ (male)"]
  LED2 = LED - 3mm [color="Green (570nm)" package="3 mm [THT]"]

nets:
  5V: R9.Pin_0, Motor_Cuttoff.COM, R2.Pin_0, D8-13.pin2, J1.pin2, C2.+, J2.pin2, R4.Pin_0, IC2.OUT, IC1.+V, BLE1.VCC, J3.pin1
  N1: R9.Pin_1, LED1.anode
  N2: Motor_Cuttoff.L2, IC1.+Vmotor, LED2.anode
  N3: R2.Pin_1, IC1.In_2, Q1.C
  RESET: C1.0, Pow.pin6
  N4: C1.1, S3.Pin_4, R7.Pin_1, BLE1.State
  VIN-Ard/Vin+: Pow.pin1, D8-13.pin1, Battery_Cuttoff.L2, C5.+, IC2.IN
  GND/GND-Ard/Gnd-Ard: Pow.pin2, Pow.pin3, D8-13.pin4, J1.pin1, C2.-, J2.pin1, C5.-, IC2.GND, S3.Pin_2, IC1.0V, R7.Pin_0, R6.Pin_1, BLE1.Gnd, -_Bat_+.2, R10.Pin_1, Q2.E, LED1.cathode, Q1.E, J3.pin2
  5V-Ard: Pow.pin4
  3.3V-Ard: Pow.pin5
  IOREF: Pow.pin7
  N5: C3.0, -_M2_+.2, IC1.Out_3_(_Controlled_by_Enable_2_)
  N6: C3.1, -_M2_+.1, IC1.Out_4_(_Controlled_by_Enable_2_)
  N7: -_M1_+.1, IC1.Out_1_(_Controlled_by_Enable_1_), C6.1
  N8: -_M1_+.2, IC1.Out_2_(_Controlled_by_Enable_1_), C6.0
  AREF: D8-13.pin3
  D13: D8-13.pin5
  D12: D8-13.pin6
  D11-PWM: D8-13.pin7
  D10-PWM: D8-13.pin8, J2.pin3
  D9-PWM: D8-13.pin9, J1.pin3
  D8/M-IN2: D8-13.pin10, R3.Pin_0, IC1.In_3
  N9: Battery_Cuttoff.COM, -_Bat_+.1
  N10: R4.Pin_1, IC1.In_4, Q2.C
  D7/M-IN1: R1.Pin_0, D0-7.pin1, IC1.In_1
  N11: R1.Pin_1, Q1.B
  A5-SCL: A0-5.pin1
  A4-SDA: A0-5.pin2
  A3: A0-5.pin3
  A2: A0-5.pin4
  A1: A0-5.pin5
  A0: A0-5.pin6
  N12: R3.Pin_1, Q2.B
  D6-PWM/M-EN2: D0-7.pin2, IC1.Enable_2
  D5-PWM/M-EN1: D0-7.pin3, IC1.Enable_1
  D4: D0-7.pin4
  D3-PWM: D0-7.pin5
  D2: D0-7.pin6
  TXD: D0-7.pin7, R13.Pin_0
  RXD: D0-7.pin8, BLE1.Txd, J3.pin3
  N13: R6.Pin_0, BLE1.Rxd, R13.Pin_1, J3.pin4
  N14: R10.Pin_0, LED2.cathode

notes:
  +Bat- | +M1- | +M2-
  A22-21.....................3-2-1
  Z
  Y
  X |-------22----------
  . 27
  . |
  .
  C
  B
  A
  NO-COM-NC

custom parts:
  HC05 Bluetooth Module: Bluetooth Module
